// Logisim project final273.circ as structural Verilog: 1 circuit, main circuit main
module main (
  input  in_1,
  input  in_2,
  input  in_3,
  input  in_4,
  input  in_5,
  input  in_6,
  input  in_7,
  input  in_8,
  input  in_9,
  input  in_10,
  input  in_11,
  input  in_12,
  input  in_13,
  input  in_14,
  input  in_15,
  input  in_16,
  input  in_17,
  output Zero,
  output Negative,
  output Overflow
);

  wire add_out, and_2_out, and_3_out, and_4_out, and_5_out, and_6_out, and_7_out, and_8_out, and_9_out,
       and_10_out, and_11_out, and_12_out, and_13_out, and_14_out, and_15_out, and_16_out, and_17_out,
       and_18_out, and_19_out, and_20_out, and_21_out, and_22_out, and_23_out, and_24_out, and_25_out,
       and_26_out, and_27_out, and_28_out, and_29_out, and_30_out, and_31_out, and_32_out, and_33_out,
       and_34_out, and_35_out, and_36_out, and_37_out, and_38_out, and_39_out, and_40_out, and_41_out,
       and_42_out, and_43_out, and_44_out, and_45_out, and_46_out, and_47_out, and_48_out, and_49_out,
       and_50_out, and_51_out, and_52_out, and_53_out, and_54_out, and_55_out, and_56_out, and_57_out,
       and_58_out, and_59_out, and_60_out, and_61_out, and_62_out, and_63_out, and_64_out, and_65_out,
       and_66_out, and_67_out, and_68_out, and_69_out, and_70_out, and_71_out, and_72_out, and_73_out,
       and_74_out, and_75_out, and_76_out, and_77_out, and_78_out, and_79_out, and_80_out, and_81_out,
       and_82_out, and_83_out, and_84_out, and_85_out, and_86_out, and_87_out, and_88_out, and_89_out,
       and_90_out, and_91_out, and_92_out, and_93_out, and_94_out, and_95_out, and_96_out, and_97_out,
       and_98_out, and_99_out, and_100_out, and_101_out, and_102_out, and_103_out, and_104_out, and_105_out,
       and_106_out, and_107_out, and_108_out, and_109_out, and_110_out, and_111_out, and_112_out,
       and_113_out, and_114_out, and_115_out, and_116_out, and_117_out, and_118_out, and_119_out,
       and_120_out, and_121_out, and_124_out, and_125_out, and_126_out, and_127_out, and_128_out,
       and_131_out, and_132_out, and_133_out, and_134_out, and_135_out, and_136_out, and_137_out,
       and_138_out, and_139_out, and_140_out, and_141_out, and_142_out, and_143_out, and_144_out,
       and_145_out, and_146_out, and_147_out, and_148_out, and_149_out, and_150_out, and_151_out,
       and_152_out, and_153_out, and_154_out, and_155_out, and_156_out, and_157_out, and_158_out,
       and_159_out, and_160_out, and_161_out, and_162_out, and_163_out, and_164_out, and_165_out,
       and_166_out, and_167_out, and_168_out, and_169_out, and_170_out, and_171_out, and_172_out,
       and_173_out, and_174_out, and_175_out, and_176_out, and_177_out, and_178_out, and_179_out,
       and_180_out, and_181_out, and_182_out, and_183_out, and_184_out, and_185_out, and_186_out,
       and_187_out, and_188_out, and_189_out, and_190_out, and_191_out, and_192_out, and_193_out,
       and_194_out, and_195_out, and_196_out, and_197_out, and_198_out, and_199_out, and_200_out,
       and_204_out, and_205_out, and_206_out, and_207_out, and_208_out, and_209_out, and_210_out,
       and_211_out, and_212_out, and_213_out, and_214_out, and_215_out, and_216_out, and_217_out,
       and_218_out, and_219_out, and_220_out, and_221_out, and_222_out, and_223_out, and_224_out,
       and_225_out, and_226_out, and_227_out, and_228_out, and_229_out, Clock, clock_1_out, CMD, d_ff_1_q,
       d_ff_2_q, d_ff_3_q, d_ff_4_q, d_ff_5_q, d_ff_6_q, d_ff_7_q, d_ff_8_q, d_ff_9_q, d_ff_10_q, d_ff_11_q,
       d_ff_12_q, d_ff_13_q, d_ff_14_q, d_ff_15_q, d_ff_16_q, d_ff_17_q, d_ff_18_q, d_ff_19_q, d_ff_20_q,
       d_ff_21_q, d_ff_22_q, d_ff_23_q, d_ff_24_q, d_ff_25_q, d_ff_26_q, d_ff_27_q, d_ff_28_q, d_ff_29_q,
       d_ff_30_q, d_ff_31_q, d_ff_32_q, d_ff_33_q, d_ff_34_q, d_ff_35_q, d_ff_36_q, d_ff_37_q, d_ff_38_q,
       d_ff_39_q, d_ff_40_q, d_ff_41_q, d_ff_42_q, d_ff_43_q, d_ff_44_q, d_ff_45_q, d_ff_46_q, d_ff_47_q,
       d_ff_48_q, d_ff_49_q, d_ff_50_q, d_ff_51_q, d_ff_52_q, d_ff_53_q, d_ff_54_q, d_ff_55_q, d_ff_56_q,
       d_ff_57_q, d_ff_58_q, d_ff_59_q, d_ff_60_q, d_ff_61_q, d_ff_62_q, d_ff_63_q, d_ff_64_q, d_ff_65_q,
       d_ff_66_q, d_ff_67_q, d_ff_68_q, d_ff_69_q, d_ff_70_q, d_ff_71_q, d_ff_72_q, d_ff_73_q, d_ff_74_q,
       d_ff_75_q, d_ff_76_q, d_ff_77_q, d_ff_78_q, d_ff_79_q, d_ff_80_q, d_ff_81_q, d_ff_82_q, d_ff_83_q,
       d_ff_84_q, d_ff_85_q, d_ff_86_q, d_ff_87_q, d_ff_88_q, d_ff_89_q, d_ff_90_q, d_ff_91_q, d_ff_92_q,
       d_ff_93_q, d_ff_94_q, d_ff_95_q, d_ff_96_q, d_ff_97_q, d_ff_98_q, d_ff_99_q, d_ff_100_q, d_ff_101_q,
       d_ff_102_q, d_ff_103_q, d_ff_104_q, d_ff_105_q, halt_out, jump_out, load_out, multiplexer_1_out,
       multiplexer_2_out, multiplexer_3_out, multiplexer_4_out, multiplexer_5_out, multiplexer_6_out,
       multiplexer_7_out, multiplexer_8_out, multiplexer_9_out, Neg_out, not_1_out, not_2_out, not_3_out,
       not_4_out, not_5_out, not_6_out, not_7_out, not_8_out, not_9_out, not_10_out, not_11_out, not_12_out,
       not_13_out, not_14_out, not_15_out, not_16_out, not_17_out, not_18_out, not_19_out, not_20_out,
       not_21_out, not_22_out, not_23_out, not_24_out, not_25_out, not_26_out, not_27_out, not_28_out,
       not_29_out, not_30_out, not_31_out, not_32_out, not_33_out, not_34_out, not_35_out, not_36_out,
       not_37_out, not_38_out, not_39_out, not_40_out, not_41_out, not_42_out, not_43_out, not_44_out,
       not_45_out, not_46_out, not_47_out, not_48_out, not_49_out, not_50_out, not_51_out, not_52_out,
       not_53_out, not_54_out, not_55_out, not_56_out, not_57_out, not_58_out, not_59_out, not_60_out,
       not_61_out, not_62_out, not_63_out, not_64_out, not_65_out, not_66_out, not_67_out, not_68_out,
       not_69_out, not_70_out, not_71_out, not_72_out, not_73_out, not_74_out, not_75_out, not_76_out,
       not_77_out, not_78_out, not_79_out, not_80_out, not_81_out, not_82_out, not_83_out, not_84_out,
       not_85_out, not_86_out, not_87_out, not_88_out, not_89_out, not_90_out, not_91_out, not_92_out,
       not_93_out, not_94_out, not_95_out, not_96_out, not_97_out, not_98_out, notZero_out, or_1_out,
       or_2_out, or_3_out, or_4_out, or_5_out, or_6_out, or_7_out, or_8_out, or_9_out, or_10_out, or_11_out,
       or_12_out, or_13_out, or_14_out, or_15_out, or_16_out, or_17_out, or_18_out, or_19_out, or_20_out,
       or_21_out, or_22_out, or_23_out, or_24_out, or_25_out, or_26_out, or_27_out, or_28_out, or_29_out,
       or_31_out, or_32_out, or_34_out, or_35_out, or_36_out, or_37_out, or_38_out, or_40_out, or_41_out,
       or_42_out, or_43_out, or_44_out, or_45_out, or_46_out, or_47_out, or_48_out, or_49_out, or_50_out,
       or_51_out, or_52_out, or_53_out, or_54_out, or_55_out, or_56_out, or_57_out, or_58_out, or_59_out,
       Pos_out, read_RAM, read_RB, save_out, sub_out, write_RAM, write_RB, xor_1_out, xor_2_out, xor_3_out,
       xor_4_out, xor_5_out, xor_6_out, xor_7_out, xor_8_out, xor_9_out, xor_10_out, xor_11_out;

  not not_1 (not_1_out, halt_out);
  and and_1 (Clock, not_1_out, clock_1_out);
  Clock clock_1 (.out(clock_1_out));
  and and_2 (and_2_out, and_121_out, Clock);
  or or_1 (or_1_out, and_2_out, and_3_out);
  D_Flip_Flop d_ff_1 (.D(d_ff_86_q), .clk(or_1_out), .Q(d_ff_1_q));  // open: Qn, preset, reset
  D_Flip_Flop d_ff_2 (.D(d_ff_87_q), .clk(or_1_out), .Q(d_ff_2_q));  // open: Qn, preset, reset
  D_Flip_Flop d_ff_3 (.D(d_ff_88_q), .clk(or_1_out), .Q(d_ff_3_q));  // open: Qn, preset, reset
  not not_2 (not_2_out, Clock);
  not not_3 (not_3_out, d_ff_61_q);
  and and_3 (and_3_out, not_2_out, d_ff_53_q, d_ff_60_q, not_3_out);
  or or_2 (or_2_out, d_ff_1_q, in_1);
  or or_3 (or_3_out, d_ff_2_q, in_2);
  or or_4 (or_4_out, d_ff_3_q, in_3);
  not not_4 (not_4_out, d_ff_61_q);
  and and_4 (and_4_out, not_4_out, not_5_out, not_6_out);
  not not_5 (not_5_out, d_ff_60_q);
  not not_6 (not_6_out, d_ff_53_q);
  and and_5 (and_5_out, in_13, 1'b1);
  D_Flip_Flop #(.trigger("falling")) d_ff_4 (.D(and_5_out), .clk(Clock), .Q(d_ff_4_q));  // open: Qn, preset, reset
  and and_6 (and_6_out, or_2_out, or_3_out, or_4_out, Clock);
  and and_7 (and_7_out, or_2_out, or_3_out, not_7_out, Clock);
  not not_7 (not_7_out, or_4_out);
  not not_8 (not_8_out, or_3_out);
  and and_8 (and_8_out, or_2_out, not_8_out, or_4_out, Clock);
  not not_9 (not_9_out, or_3_out);
  and and_9 (and_9_out, or_2_out, not_9_out, not_10_out, Clock);
  not not_10 (not_10_out, or_4_out);
  not not_11 (not_11_out, or_2_out);
  and and_10 (and_10_out, not_11_out, or_3_out, or_4_out, Clock);
  not not_12 (not_12_out, or_2_out);
  and and_11 (and_11_out, not_12_out, or_3_out, not_13_out, Clock);
  not not_13 (not_13_out, or_4_out);
  not not_14 (not_14_out, or_2_out);
  not not_15 (not_15_out, or_3_out);
  and and_12 (and_12_out, not_14_out, not_15_out, or_4_out, Clock);
  not not_16 (not_16_out, or_2_out);
  not not_17 (not_17_out, or_3_out);
  and and_13 (and_13_out, not_16_out, not_17_out, not_18_out, Clock);
  not not_18 (not_18_out, or_4_out);
  and and_14 (and_14_out, and_6_out, not_19_out);
  and and_15 (and_15_out, and_7_out, not_19_out);
  and and_16 (and_16_out, and_8_out, not_19_out);
  and and_17 (and_17_out, and_9_out, not_19_out);
  and and_18 (and_18_out, and_10_out, not_19_out);
  and and_19 (and_19_out, and_11_out, not_19_out);
  and and_20 (and_20_out, and_12_out, not_19_out);
  and and_21 (and_21_out, and_13_out, not_19_out);
  not not_19 (not_19_out, d_ff_5_q);
  D_Flip_Flop d_ff_5 (.D(in_13), .clk(Clock), .Q(d_ff_5_q));  // open: Qn, preset, reset
  and and_22 (and_22_out, and_6_out, not_19_out, d_ff_14_q);
  and and_23 (and_23_out, and_7_out, not_19_out, d_ff_14_q);
  and and_24 (and_24_out, and_8_out, not_19_out, d_ff_14_q);
  and and_25 (and_25_out, and_9_out, not_19_out, d_ff_14_q);
  and and_26 (and_26_out, and_10_out, not_19_out, d_ff_14_q);
  and and_27 (and_27_out, and_11_out, not_19_out, d_ff_14_q);
  and and_28 (and_28_out, and_12_out, not_19_out, d_ff_14_q);
  and and_29 (and_29_out, and_13_out, not_19_out, d_ff_14_q);
  Multiplexer #(.enable("false")) multiplexer_1 (.in0(1'b0), .in1(1'b1), .out(multiplexer_1_out), .sel(and_4_out));
  D_Flip_Flop #(.trigger("high")) d_ff_6 (.D(and_22_out), .clk(and_14_out), .Q(d_ff_6_q));  // open: Qn, preset, reset
  D_Flip_Flop #(.trigger("high")) d_ff_7 (.D(and_23_out), .clk(and_15_out), .Q(d_ff_7_q));  // open: Qn, preset, reset
  D_Flip_Flop #(.trigger("high")) d_ff_8 (.D(and_24_out), .clk(and_16_out), .Q(d_ff_8_q));  // open: Qn, preset, reset
  D_Flip_Flop #(.trigger("high")) d_ff_9 (.D(and_25_out), .clk(and_17_out), .Q(d_ff_9_q));  // open: Qn, preset, reset
  D_Flip_Flop #(.trigger("high")) d_ff_10 (.D(and_26_out), .clk(and_18_out), .Q(d_ff_10_q));  // open: Qn, preset, reset
  D_Flip_Flop #(.trigger("high")) d_ff_11 (.D(and_27_out), .clk(and_19_out), .Q(d_ff_11_q));  // open: Qn, preset, reset
  D_Flip_Flop #(.trigger("high")) d_ff_12 (.D(and_28_out), .clk(and_20_out), .Q(d_ff_12_q));  // open: Qn, preset, reset
  D_Flip_Flop #(.trigger("high")) d_ff_13 (.D(and_29_out), .clk(and_21_out), .Q(d_ff_13_q));  // open: Qn, preset, reset
  and and_30 (and_30_out, or_4_out, multiplexer_1_out);
  or or_5 (or_5_out, multiplexer_1_out, or_4_out);
  or or_6 (or_6_out, and_31_out, and_32_out, and_33_out, and_34_out, and_35_out, and_36_out, and_37_out, and_38_out);
  and and_31 (and_31_out, d_ff_6_q, and_6_out, d_ff_5_q);
  and and_32 (and_32_out, d_ff_7_q, and_7_out, d_ff_5_q);
  and and_33 (and_33_out, d_ff_8_q, and_8_out, d_ff_5_q);
  and and_34 (and_34_out, d_ff_9_q, and_9_out, d_ff_5_q);
  and and_35 (and_35_out, d_ff_10_q, and_10_out, d_ff_5_q);
  and and_36 (and_36_out, d_ff_11_q, and_11_out, d_ff_5_q);
  and and_37 (and_37_out, d_ff_12_q, and_12_out, d_ff_5_q);
  and and_38 (and_38_out, d_ff_13_q, and_13_out, d_ff_5_q);
  D_Flip_Flop d_ff_14 (.D(in_14), .clk(Clock), .Q(d_ff_14_q));  // open: Qn, preset, reset
  or or_7 (or_7_out, or_3_out, and_30_out);
  not not_20 (not_20_out, and_30_out);
  D_Flip_Flop d_ff_15 (.D(in_15), .clk(Clock), .Q(d_ff_15_q));  // open: Qn, preset, reset
  not not_21 (not_21_out, and_39_out);
  and and_39 (and_39_out, and_30_out, or_3_out);
  and and_40 (and_40_out, not_20_out, or_5_out);
  and and_41 (and_41_out, and_6_out, not_19_out, d_ff_15_q);
  D_Flip_Flop #(.trigger("high")) d_ff_16 (.D(and_41_out), .clk(and_14_out), .Q(d_ff_16_q));  // open: Qn, preset, reset
  D_Flip_Flop #(.trigger("high")) d_ff_17 (.D(and_42_out), .clk(and_15_out), .Q(d_ff_17_q));  // open: Qn, preset, reset
  and and_42 (and_42_out, and_7_out, not_19_out, d_ff_15_q);
  D_Flip_Flop #(.trigger("high")) d_ff_18 (.D(and_43_out), .clk(and_16_out), .Q(d_ff_18_q));  // open: Qn, preset, reset
  and and_43 (and_43_out, and_8_out, not_19_out, d_ff_15_q);
  D_Flip_Flop #(.trigger("high")) d_ff_19 (.D(and_44_out), .clk(and_17_out), .Q(d_ff_19_q));  // open: Qn, preset, reset
  and and_44 (and_44_out, and_9_out, not_19_out, d_ff_15_q);
  and and_45 (and_45_out, and_10_out, not_19_out, d_ff_15_q);
  D_Flip_Flop #(.trigger("high")) d_ff_20 (.D(and_45_out), .clk(and_18_out), .Q(d_ff_20_q));  // open: Qn, preset, reset
  D_Flip_Flop #(.trigger("high")) d_ff_21 (.D(and_46_out), .clk(and_19_out), .Q(d_ff_21_q));  // open: Qn, preset, reset
  and and_46 (and_46_out, and_11_out, not_19_out, d_ff_15_q);
  D_Flip_Flop #(.trigger("high")) d_ff_22 (.D(and_47_out), .clk(and_20_out), .Q(d_ff_22_q));  // open: Qn, preset, reset
  and and_47 (and_47_out, and_12_out, not_19_out, d_ff_15_q);
  D_Flip_Flop #(.trigger("high")) d_ff_23 (.D(and_48_out), .clk(and_21_out), .Q(d_ff_23_q));  // open: Qn, preset, reset
  and and_48 (and_48_out, and_13_out, not_19_out, d_ff_15_q);
  D_Flip_Flop d_ff_24 (.D(in_16), .clk(Clock), .Q(d_ff_24_q));  // open: Qn, preset, reset
  and and_49 (and_49_out, and_39_out, or_2_out);
  not not_22 (not_22_out, and_49_out);
  or or_8 (or_8_out, or_2_out, and_39_out);
  and and_50 (and_50_out, not_21_out, or_7_out);
  or or_9 (or_9_out, and_51_out, and_52_out, and_53_out, and_54_out, and_55_out, and_56_out, and_57_out, and_58_out);
  and and_51 (and_51_out, d_ff_16_q, and_6_out, d_ff_5_q);
  and and_52 (and_52_out, d_ff_17_q, and_7_out, d_ff_5_q);
  and and_53 (and_53_out, d_ff_18_q, and_8_out, d_ff_5_q);
  and and_54 (and_54_out, d_ff_19_q, and_9_out, d_ff_5_q);
  and and_55 (and_55_out, d_ff_20_q, and_10_out, d_ff_5_q);
  and and_56 (and_56_out, d_ff_21_q, and_11_out, d_ff_5_q);
  and and_57 (and_57_out, d_ff_22_q, and_12_out, d_ff_5_q);
  and and_58 (and_58_out, d_ff_23_q, and_13_out, d_ff_5_q);
  D_Flip_Flop d_ff_25 (.D(in_17), .clk(Clock), .Q(d_ff_25_q));  // open: Qn, preset, reset
  and and_59 (and_59_out, not_22_out, or_8_out);
  D_Flip_Flop #(.trigger("high")) d_ff_26 (.D(and_60_out), .clk(and_14_out), .Q(d_ff_26_q));  // open: Qn, preset, reset
  and and_60 (and_60_out, and_6_out, not_19_out, d_ff_24_q);
  D_Flip_Flop #(.trigger("high")) d_ff_27 (.D(and_61_out), .clk(and_15_out), .Q(d_ff_27_q));  // open: Qn, preset, reset
  and and_61 (and_61_out, and_7_out, not_19_out, d_ff_24_q);
  and and_62 (and_62_out, and_8_out, not_19_out, d_ff_24_q);
  D_Flip_Flop #(.trigger("high")) d_ff_28 (.D(and_62_out), .clk(and_16_out), .Q(d_ff_28_q));  // open: Qn, preset, reset
  D_Flip_Flop #(.trigger("high")) d_ff_29 (.D(and_63_out), .clk(and_17_out), .Q(d_ff_29_q));  // open: Qn, preset, reset
  and and_63 (and_63_out, and_9_out, not_19_out, d_ff_24_q);
  and and_64 (and_64_out, and_10_out, not_19_out, d_ff_24_q);
  D_Flip_Flop #(.trigger("high")) d_ff_30 (.D(and_64_out), .clk(and_18_out), .Q(d_ff_30_q));  // open: Qn, preset, reset
  and and_65 (and_65_out, and_11_out, not_19_out, d_ff_24_q);
  D_Flip_Flop #(.trigger("high")) d_ff_31 (.D(and_65_out), .clk(and_19_out), .Q(d_ff_31_q));  // open: Qn, preset, reset
  and and_66 (and_66_out, and_12_out, not_19_out, d_ff_24_q);
  D_Flip_Flop #(.trigger("high")) d_ff_32 (.D(and_66_out), .clk(and_20_out), .Q(d_ff_32_q));  // open: Qn, preset, reset
  and and_67 (and_67_out, and_13_out, not_19_out, d_ff_24_q);
  D_Flip_Flop #(.trigger("high")) d_ff_33 (.D(and_67_out), .clk(and_21_out), .Q(d_ff_33_q));  // open: Qn, preset, reset
  or or_10 (or_10_out, and_68_out, and_69_out, and_70_out, and_71_out, and_72_out, and_73_out, and_74_out, and_75_out);
  and and_68 (and_68_out, d_ff_26_q, and_6_out, d_ff_5_q);
  and and_69 (and_69_out, d_ff_27_q, and_7_out, d_ff_5_q);
  and and_70 (and_70_out, d_ff_28_q, and_8_out, d_ff_5_q);
  and and_71 (and_71_out, d_ff_29_q, and_9_out, d_ff_5_q);
  and and_72 (and_72_out, d_ff_30_q, and_10_out, d_ff_5_q);
  and and_73 (and_73_out, d_ff_31_q, and_11_out, d_ff_5_q);
  and and_74 (and_74_out, d_ff_32_q, and_12_out, d_ff_5_q);
  and and_75 (and_75_out, d_ff_33_q, and_13_out, d_ff_5_q);
  D_Flip_Flop #(.trigger("high")) d_ff_34 (.D(and_76_out), .clk(and_14_out), .Q(d_ff_34_q));  // open: Qn, preset, reset
  and and_76 (and_76_out, and_6_out, not_19_out, d_ff_25_q);
  and and_77 (and_77_out, and_7_out, not_19_out, d_ff_25_q);
  D_Flip_Flop #(.trigger("high")) d_ff_35 (.D(and_77_out), .clk(and_15_out), .Q(d_ff_35_q));  // open: Qn, preset, reset
  and and_78 (and_78_out, and_8_out, not_19_out, d_ff_25_q);
  D_Flip_Flop #(.trigger("high")) d_ff_36 (.D(and_78_out), .clk(and_16_out), .Q(d_ff_36_q));  // open: Qn, preset, reset
  D_Flip_Flop #(.trigger("high")) d_ff_37 (.D(and_79_out), .clk(and_17_out), .Q(d_ff_37_q));  // open: Qn, preset, reset
  and and_79 (and_79_out, and_9_out, not_19_out, d_ff_25_q);
  D_Flip_Flop #(.trigger("high")) d_ff_38 (.D(and_80_out), .clk(and_18_out), .Q(d_ff_38_q));  // open: Qn, preset, reset
  and and_80 (and_80_out, and_10_out, not_19_out, d_ff_25_q);
  and and_81 (and_81_out, and_11_out, not_19_out, d_ff_25_q);
  D_Flip_Flop #(.trigger("high")) d_ff_39 (.D(and_81_out), .clk(and_19_out), .Q(d_ff_39_q));  // open: Qn, preset, reset
  and and_82 (and_82_out, and_12_out, not_19_out, d_ff_25_q);
  D_Flip_Flop #(.trigger("high")) d_ff_40 (.D(and_82_out), .clk(and_20_out), .Q(d_ff_40_q));  // open: Qn, preset, reset
  and and_83 (and_83_out, and_13_out, not_19_out, d_ff_25_q);
  D_Flip_Flop #(.trigger("high")) d_ff_41 (.D(and_83_out), .clk(and_21_out), .Q(d_ff_41_q));  // open: Qn, preset, reset
  or or_11 (or_11_out, and_84_out, and_85_out, and_86_out, and_87_out, and_88_out, and_89_out, and_90_out, and_91_out);
  and and_84 (and_84_out, d_ff_34_q, and_6_out, d_ff_5_q);
  and and_85 (and_85_out, d_ff_35_q, and_7_out, d_ff_5_q);
  and and_86 (and_86_out, d_ff_36_q, and_8_out, d_ff_5_q);
  and and_87 (and_87_out, d_ff_37_q, and_9_out, d_ff_5_q);
  and and_88 (and_88_out, d_ff_38_q, and_10_out, d_ff_5_q);
  and and_89 (and_89_out, d_ff_39_q, and_11_out, d_ff_5_q);
  and and_90 (and_90_out, d_ff_40_q, and_12_out, d_ff_5_q);
  and and_91 (and_91_out, d_ff_41_q, and_13_out, d_ff_5_q);
  or or_12 (or_12_out, and_96_out, or_35_out, and_92_out);
  and and_92 (and_92_out, or_25_out, Clock);
  or or_13 (or_13_out, multiplexer_2_out, in_9);
  Multiplexer #(.enable("false")) multiplexer_2 (
    .in0(d_ff_102_q), .in1(d_ff_76_q), .out(multiplexer_2_out), .sel(or_15_out));
  and and_93 (and_93_out, not_26_out, d_ff_4_q);
  D_Flip_Flop #(.trigger("falling")) d_ff_42 (.D(or_6_out), .clk(Clock), .Q(d_ff_42_q));  // open: Qn, preset, reset
  D_Flip_Flop #(.trigger("falling")) d_ff_43 (.D(or_9_out), .clk(Clock), .Q(d_ff_43_q));  // open: Qn, preset, reset
  D_Flip_Flop #(.trigger("falling")) d_ff_44 (.D(or_10_out), .clk(Clock), .Q(d_ff_44_q));  // open: Qn, preset, reset
  D_Flip_Flop #(.trigger("falling")) d_ff_45 (.D(or_11_out), .clk(Clock), .Q(d_ff_45_q));  // open: Qn, preset, reset
  and and_94 (and_94_out, write_RB, not_27_out, d_ff_50_q);
  and and_95 (and_95_out, write_RB, not_27_out, not_23_out);
  not not_23 (not_23_out, d_ff_50_q);
  and and_96 (and_96_out, Clock, not_34_out);
  D_Flip_Flop d_ff_46 (.D(or_13_out), .clk(or_12_out), .Q(d_ff_46_q));  // open: Qn, preset, reset
  Multiplexer #(.enable("false")) multiplexer_3 (
    .in0(d_ff_103_q), .in1(d_ff_77_q), .out(multiplexer_3_out), .sel(or_15_out));
  not not_24 (not_24_out, d_ff_53_q);
  and and_97 (and_97_out, not_24_out, Clock);
  D_Flip_Flop d_ff_47 (.D(or_14_out), .clk(or_12_out), .Q(d_ff_47_q));  // open: Qn, preset, reset
  or or_14 (or_14_out, multiplexer_3_out, in_10);
  Multiplexer #(.enable("false")) multiplexer_4 (
    .in0(d_ff_104_q), .in1(d_ff_84_q), .out(multiplexer_4_out), .sel(or_15_out));
  not not_25 (not_25_out, d_ff_57_q);
  and and_98 (and_98_out, d_ff_55_q, not_25_out);
  and and_99 (and_99_out, d_ff_55_q, d_ff_57_q);
  or or_15 (or_15_out, and_98_out, and_99_out);
  D_Flip_Flop d_ff_48 (.D(d_ff_42_q), .clk(and_97_out), .Q(d_ff_48_q));  // open: Qn, preset, reset
  D_Flip_Flop d_ff_49 (.D(d_ff_43_q), .clk(and_97_out), .Q(d_ff_49_q));  // open: Qn, preset, reset
  D_Flip_Flop d_ff_50 (.D(d_ff_44_q), .clk(and_97_out), .Q(d_ff_50_q));  // open: Qn, preset, reset
  D_Flip_Flop d_ff_51 (.D(d_ff_45_q), .clk(and_97_out), .Q(d_ff_51_q));  // open: Qn, preset, reset
  D_Flip_Flop d_ff_52 (.D(or_16_out), .clk(or_12_out), .Q(d_ff_52_q));  // open: Qn, preset, reset
  or or_16 (or_16_out, multiplexer_4_out, in_11);
  Multiplexer #(.enable("false")) multiplexer_5 (
    .in0(d_ff_105_q), .in1(d_ff_85_q), .out(multiplexer_5_out), .sel(or_15_out));
  and and_100 (and_100_out, d_ff_61_q, d_ff_60_q);
  not not_26 (not_26_out, and_100_out);
  D_Flip_Flop d_ff_53 (.D(and_93_out), .clk(Clock), .Q(d_ff_53_q));  // open: Qn, preset, reset
  not not_27 (not_27_out, and_101_out);
  and and_101 (and_101_out, not_29_out, not_28_out);
  not not_28 (not_28_out, d_ff_51_q);
  not not_29 (not_29_out, d_ff_50_q);
  and and_102 (and_102_out, Clock, d_ff_51_q);
  and and_103 (and_103_out, Clock, d_ff_50_q);
  not not_30 (not_30_out, and_103_out);
  not not_31 (not_31_out, and_102_out);
  D_Flip_Flop d_ff_54 (.D(or_17_out), .clk(or_12_out), .Q(d_ff_54_q));  // open: Qn, preset, reset
  or or_17 (or_17_out, multiplexer_5_out, in_12);
  not not_32 (not_32_out, d_ff_53_q);
  D_Flip_Flop d_ff_55 (.D(d_ff_48_q), .clk(Clock), .Q(d_ff_55_q));  // open: Qn, preset, reset
  not not_33 (not_33_out, write_RB);
  or or_18 (or_18_out, read_RB, not_33_out);
  D_Flip_Flop d_ff_56 (.D(or_18_out), .clk(or_20_out), .Q(d_ff_56_q));  // open: Qn, preset, reset
  or or_19 (or_19_out, write_RB, read_RB);
  and and_104 (and_104_out, Clock, or_19_out);
  or or_20 (or_20_out, and_104_out, and_113_out);
  not not_34 (not_34_out, d_ff_56_q);
  D_Flip_Flop d_ff_57 (.D(d_ff_49_q), .clk(Clock), .Q(d_ff_57_q));  // open: Qn, preset, reset
  D_Flip_Flop d_ff_58 (.D(and_105_out), .clk(and_106_out), .Q(d_ff_58_q));  // open: Qn, preset, reset
  buf and_105 (and_105_out, d_ff_46_q);  // AND_Gate
  buf and_106 (and_106_out, and_94_out);  // AND_Gate
  D_Flip_Flop d_ff_59 (.D(and_107_out), .clk(and_108_out), .Q(d_ff_59_q));  // open: Qn, preset, reset
  buf and_107 (and_107_out, d_ff_46_q);  // AND_Gate
  buf and_108 (and_108_out, and_95_out);  // AND_Gate
  not not_35 (not_35_out, d_ff_57_q);
  not not_36 (not_36_out, d_ff_55_q);
  and jump (jump_out, not_35_out, not_36_out, d_ff_53_q, not_37_out, not_38_out);
  not not_37 (not_37_out, d_ff_50_q);
  not not_38 (not_38_out, d_ff_51_q);
  not not_39 (not_39_out, d_ff_57_q);
  not not_40 (not_40_out, d_ff_55_q);
  and load (load_out, not_39_out, not_40_out, not_27_out, d_ff_53_q);
  not not_41 (not_41_out, d_ff_55_q);
  and save (save_out, d_ff_57_q, not_41_out, d_ff_53_q);
  not not_42 (not_42_out, d_ff_57_q);
  and add (add_out, not_42_out, d_ff_55_q, d_ff_53_q);
  and sub (sub_out, d_ff_57_q, d_ff_55_q, d_ff_53_q);
  and halt (halt_out, d_ff_57_q, d_ff_55_q, d_ff_53_q, d_ff_51_q, d_ff_50_q);
  or or_21 (or_21_out, and_109_out, and_110_out);
  and and_109 (and_109_out, and_103_out, d_ff_56_q, d_ff_58_q);
  and and_110 (and_110_out, not_30_out, d_ff_56_q, d_ff_59_q);
  D_Flip_Flop d_ff_60 (.D(and_153_out), .clk(Clock), .Q(d_ff_60_q));  // open: Qn, preset, reset
  not not_43 (not_43_out, d_ff_57_q);
  not not_44 (not_44_out, d_ff_55_q);
  not not_45 (not_45_out, d_ff_49_q);
  or or_22 (or_22_out, and_111_out, and_112_out);
  and and_111 (and_111_out, and_102_out, d_ff_56_q, d_ff_58_q);
  not not_46 (not_46_out, d_ff_56_q);
  and and_112 (and_112_out, not_31_out, d_ff_56_q, d_ff_59_q);
  D_Flip_Flop d_ff_61 (.D(and_151_out), .clk(Clock), .Q(d_ff_61_q));  // open: Qn, preset, reset
  and and_113 (and_113_out, not_43_out, not_44_out, d_ff_48_q, not_45_out);
  buf and_114 (and_114_out, d_ff_47_q);  // AND_Gate
  buf and_115 (and_115_out, and_94_out);  // AND_Gate
  buf and_116 (and_116_out, d_ff_47_q);  // AND_Gate
  or or_23 (or_23_out, and_117_out, and_141_out);
  and and_117 (and_117_out, and_103_out, d_ff_56_q, d_ff_62_q);
  D_Flip_Flop d_ff_62 (.D(and_114_out), .clk(and_115_out), .Q(d_ff_62_q));  // open: Qn, preset, reset
  D_Flip_Flop d_ff_63 (.D(and_116_out), .clk(and_118_out), .Q(d_ff_63_q));  // open: Qn, preset, reset
  buf and_118 (and_118_out, and_95_out);  // AND_Gate
  Multiplexer #(.enable("false")) multiplexer_6 (.in0(1'b1), .in1(1'b0), .out(multiplexer_6_out), .sel(not_32_out));
  not not_47 (not_47_out, d_ff_61_q);
  and and_119 (and_119_out, jump_out, not_47_out, not_48_out);
  not not_48 (not_48_out, d_ff_60_q);
  and and_120 (and_120_out, jump_out, d_ff_61_q, not_49_out);
  not not_49 (not_49_out, d_ff_60_q);
  and and_121 (and_121_out, jump_out, not_50_out, d_ff_60_q);
  not not_50 (not_50_out, d_ff_61_q);
  // AND_Gate and_122 has open pins: in0=jump_out, in1=d_ff_61_q, in2=d_ff_60_q, out=open
  and and_123 (read_RAM, load_out, not_51_out, not_52_out);
  not not_51 (not_51_out, d_ff_61_q);
  not not_52 (not_52_out, d_ff_60_q);
  and and_124 (and_124_out, load_out, d_ff_61_q, not_53_out);
  not not_53 (not_53_out, d_ff_60_q);
  not not_54 (not_54_out, d_ff_61_q);
  and and_125 (and_125_out, load_out, not_54_out, d_ff_60_q);
  and and_126 (and_126_out, load_out, d_ff_61_q, d_ff_60_q);
  not not_55 (not_55_out, d_ff_61_q);
  and and_127 (and_127_out, save_out, not_55_out, not_56_out);
  not not_56 (not_56_out, d_ff_60_q);
  and and_128 (and_128_out, save_out, d_ff_61_q, not_57_out);
  not not_57 (not_57_out, d_ff_60_q);
  not not_58 (not_58_out, d_ff_61_q);
  and and_129 (write_RAM, save_out, not_58_out, d_ff_60_q);
  // AND_Gate and_130 has open pins: in0=save_out, in1=d_ff_61_q, in2=d_ff_60_q, out=open
  and and_131 (and_131_out, add_out, not_59_out, not_60_out);
  not not_59 (not_59_out, d_ff_61_q);
  not not_60 (not_60_out, d_ff_60_q);
  and and_132 (and_132_out, add_out, d_ff_61_q, not_61_out);
  not not_61 (not_61_out, d_ff_60_q);
  and and_133 (and_133_out, add_out, not_62_out, d_ff_60_q);
  not not_62 (not_62_out, d_ff_61_q);
  and and_134 (and_134_out, add_out, d_ff_61_q, d_ff_60_q);
  and and_135 (and_135_out, sub_out, not_63_out, not_64_out);
  not not_63 (not_63_out, d_ff_61_q);
  not not_64 (not_64_out, d_ff_60_q);
  and and_136 (and_136_out, sub_out, d_ff_61_q, not_65_out);
  not not_65 (not_65_out, d_ff_60_q);
  not not_66 (not_66_out, d_ff_61_q);
  and and_137 (and_137_out, sub_out, not_66_out, d_ff_60_q);
  and and_138 (and_138_out, sub_out, d_ff_61_q, d_ff_60_q);
  or or_24 (or_24_out, and_139_out, and_140_out);
  and and_139 (and_139_out, and_102_out, d_ff_56_q, d_ff_62_q);
  and and_140 (and_140_out, not_31_out, d_ff_56_q, d_ff_63_q);
  and and_141 (and_141_out, not_30_out, d_ff_56_q, d_ff_63_q);
  or or_25 (or_25_out, and_137_out, and_133_out);
  buf and_142 (and_142_out, d_ff_52_q);  // AND_Gate
  not not_67 (not_67_out, d_ff_56_q);
  or or_26 (or_26_out, multiplexer_6_out, d_ff_61_q);
  and and_143 (and_143_out, multiplexer_6_out, d_ff_61_q);
  D_Flip_Flop d_ff_64 (.D(and_142_out), .clk(and_144_out), .Q(d_ff_64_q));  // open: Qn, preset, reset
  buf and_144 (and_144_out, and_94_out);  // AND_Gate
  D_Flip_Flop d_ff_65 (.D(and_145_out), .clk(and_146_out), .Q(d_ff_65_q));  // open: Qn, preset, reset
  buf and_145 (and_145_out, d_ff_52_q);  // AND_Gate
  buf and_146 (and_146_out, and_95_out);  // AND_Gate
  not not_68 (not_68_out, and_143_out);
  or or_27 (or_27_out, and_143_out, d_ff_60_q);
  and and_147 (and_147_out, and_143_out, d_ff_60_q);
  or or_28 (or_28_out, and_149_out, and_150_out);
  or or_29 (or_29_out, and_148_out, and_152_out);
  and and_148 (and_148_out, and_102_out, d_ff_56_q, d_ff_64_q);
  and and_149 (and_149_out, and_103_out, d_ff_56_q, d_ff_64_q);
  and and_150 (and_150_out, not_30_out, d_ff_56_q, d_ff_65_q);
  and and_151 (and_151_out, or_26_out, not_68_out);
  not not_69 (not_69_out, and_147_out);
  not not_70 (not_70_out, d_ff_60_q);
  or or_30 (write_RB, and_126_out, and_134_out, and_138_out);
  or or_31 (or_31_out, and_124_out, and_134_out, and_125_out, and_138_out);
  not not_71 (not_71_out, d_ff_56_q);
  and and_152 (and_152_out, not_31_out, d_ff_56_q, d_ff_65_q);
  and and_153 (and_153_out, or_27_out, not_69_out);
  and and_154 (and_154_out, d_ff_61_q, not_70_out, Clock);
  or or_32 (or_32_out, and_131_out, and_136_out);
  or or_33 (read_RB, and_119_out, and_127_out, and_131_out, and_135_out);
  D_Flip_Flop d_ff_66 (.D(and_155_out), .clk(and_156_out), .Q(d_ff_66_q));  // open: Qn, preset, reset
  buf and_155 (and_155_out, d_ff_54_q);  // AND_Gate
  buf and_156 (and_156_out, and_94_out);  // AND_Gate
  D_Flip_Flop #(.trigger("high")) d_ff_67 (
    .D(and_157_out), .clk(and_158_out), .Q(d_ff_67_q));  // open: Qn, preset, reset
  buf and_157 (and_157_out, d_ff_54_q);  // AND_Gate
  buf and_158 (and_158_out, and_95_out);  // AND_Gate
  or or_34 (or_34_out, and_159_out, and_160_out);
  and and_159 (and_159_out, and_103_out, d_ff_56_q, d_ff_66_q);
  and and_160 (and_160_out, not_30_out, d_ff_56_q, d_ff_67_q);
  buf or_35 (or_35_out, and_124_out);  // OR_Gate
  or or_36 (or_36_out, and_161_out, and_162_out);
  and and_161 (and_161_out, and_102_out, d_ff_56_q, d_ff_66_q);
  and and_162 (and_162_out, not_31_out, d_ff_56_q, d_ff_67_q);
  D_Flip_Flop #(.trigger("falling")) d_ff_68 (.D(or_21_out), .clk(Clock), .Q(d_ff_68_q));  // open: Qn, preset, reset
  D_Flip_Flop #(.trigger("falling")) d_ff_69 (.D(or_23_out), .clk(Clock), .Q(d_ff_69_q));  // open: Qn, preset, reset
  D_Flip_Flop #(.trigger("falling")) d_ff_70 (.D(or_28_out), .clk(Clock), .Q(d_ff_70_q));  // open: Qn, preset, reset
  D_Flip_Flop #(.trigger("falling")) d_ff_71 (.D(or_34_out), .clk(Clock), .Q(d_ff_71_q));  // open: Qn, preset, reset
  D_Flip_Flop #(.trigger("falling")) d_ff_72 (.D(or_22_out), .clk(Clock), .Q(d_ff_72_q));  // open: Qn, preset, reset
  D_Flip_Flop #(.trigger("falling")) d_ff_73 (.D(or_24_out), .clk(Clock), .Q(d_ff_73_q));  // open: Qn, preset, reset
  D_Flip_Flop #(.trigger("falling")) d_ff_74 (.D(or_29_out), .clk(Clock), .Q(d_ff_74_q));  // open: Qn, preset, reset
  D_Flip_Flop #(.trigger("falling")) d_ff_75 (.D(or_36_out), .clk(Clock), .Q(d_ff_75_q));  // open: Qn, preset, reset
  or or_37 (or_37_out, and_132_out, and_136_out);
  or or_38 (or_38_out, and_136_out, and_132_out);
  and and_163 (and_163_out, Clock, or_38_out);
  not not_72 (not_72_out, and_132_out);
  or or_39 (CMD, not_72_out, and_136_out);
  and and_164 (and_164_out, and_168_out, or_43_out);
  and and_165 (and_165_out, xor_1_out, or_41_out);
  or or_40 (or_40_out, and_164_out, and_165_out);
  D_Flip_Flop #(.trigger("falling")) d_ff_76 (
    .D(xor_2_out), .clk(and_163_out), .Q(d_ff_76_q));  // open: Qn, preset, reset
  and and_166 (and_166_out, and_120_out, Clock);
  not not_73 (not_73_out, CMD);
  xor xor_1 (xor_1_out, and_168_out, or_43_out);
  xor xor_2 (xor_2_out, xor_1_out, or_41_out);
  and and_167 (and_167_out, and_4_out, not_74_out);
  not not_74 (not_74_out, Clock);
  and and_168 (and_168_out, d_ff_68_q, or_37_out);
  and and_169 (and_169_out, or_44_out, and_172_out);
  and and_170 (and_170_out, xor_3_out, or_42_out);
  or or_41 (or_41_out, and_169_out, and_170_out);
  D_Flip_Flop #(.trigger("falling")) d_ff_77 (
    .D(xor_4_out), .clk(and_163_out), .Q(d_ff_77_q));  // open: Qn, preset, reset
  and and_171 (and_171_out, d_ff_71_q, or_37_out);
  and and_172 (and_172_out, d_ff_69_q, or_37_out);
  and and_173 (and_173_out, d_ff_70_q, or_37_out);
  xor xor_3 (xor_3_out, and_172_out, or_44_out);
  xor xor_4 (xor_4_out, xor_3_out, or_42_out);
  D_Flip_Flop d_ff_78 (.D(and_59_out), .clk(and_167_out), .Q(d_ff_78_q));  // open: Qn, preset, reset
  D_Flip_Flop d_ff_79 (.D(and_50_out), .clk(and_167_out), .Q(d_ff_79_q));  // open: Qn, preset, reset
  D_Flip_Flop d_ff_80 (.D(and_40_out), .clk(and_167_out), .Q(d_ff_80_q));  // open: Qn, preset, reset
  D_Flip_Flop d_ff_81 (.D(d_ff_69_q), .clk(and_166_out), .Q(d_ff_81_q));  // open: Qn, preset, reset
  D_Flip_Flop d_ff_82 (.D(d_ff_70_q), .clk(and_166_out), .Q(d_ff_82_q));  // open: Qn, preset, reset
  D_Flip_Flop d_ff_83 (.D(d_ff_71_q), .clk(and_166_out), .Q(d_ff_83_q));  // open: Qn, preset, reset
  xor xor_5 (xor_5_out, and_173_out, or_46_out);
  and and_174 (and_174_out, and_173_out, or_46_out);
  and and_175 (and_175_out, xor_5_out, and_176_out);
  or or_42 (or_42_out, and_174_out, and_175_out);
  D_Flip_Flop #(.trigger("falling")) d_ff_84 (
    .D(xor_6_out), .clk(and_163_out), .Q(d_ff_84_q));  // open: Qn, preset, reset
  or or_43 (or_43_out, xor_8_out, and_179_out);
  or or_44 (or_44_out, xor_9_out, and_178_out);
  and and_176 (and_176_out, and_171_out, or_45_out);
  xor xor_6 (xor_6_out, xor_5_out, and_176_out);
  D_Flip_Flop #(.trigger("falling")) d_ff_85 (
    .D(xor_7_out), .clk(and_163_out), .Q(d_ff_85_q));  // open: Qn, preset, reset
  Multiplexer #(.enable("false")) multiplexer_7 (
    .in0(d_ff_78_q), .in1(d_ff_81_q), .out(multiplexer_7_out), .sel(and_120_out));
  Multiplexer #(.enable("false")) multiplexer_8 (
    .in0(d_ff_79_q), .in1(d_ff_82_q), .out(multiplexer_8_out), .sel(and_120_out));
  Multiplexer #(.enable("false")) multiplexer_9 (
    .in0(d_ff_80_q), .in1(d_ff_83_q), .out(multiplexer_9_out), .sel(and_120_out));
  and and_177 (and_177_out, and_120_out, Clock);
  or or_45 (or_45_out, xor_11_out, and_182_out);
  or or_46 (or_46_out, xor_10_out, and_181_out);
  xor xor_7 (xor_7_out, and_171_out, or_45_out);
  D_Flip_Flop d_ff_86 (.D(multiplexer_7_out), .clk(or_47_out), .Q(d_ff_86_q));  // open: Qn, preset, reset
  D_Flip_Flop d_ff_87 (.D(multiplexer_8_out), .clk(or_47_out), .Q(d_ff_87_q));  // open: Qn, preset, reset
  D_Flip_Flop d_ff_88 (.D(multiplexer_9_out), .clk(or_47_out), .Q(d_ff_88_q));  // open: Qn, preset, reset
  or or_47 (or_47_out, and_177_out, and_154_out);
  and and_178 (and_178_out, and_187_out, not_73_out);
  and and_179 (and_179_out, and_185_out, not_73_out);
  xor xor_8 (xor_8_out, not_79_out, and_183_out);
  and and_180 (and_180_out, not_79_out, and_183_out);
  not not_75 (not_75_out, xor_7_out);
  not not_76 (not_76_out, xor_6_out);
  not not_77 (not_77_out, xor_4_out);
  not not_78 (not_78_out, xor_2_out);
  and and_181 (and_181_out, and_186_out, not_73_out);
  and and_182 (and_182_out, and_192_out, not_73_out);
  xor xor_9 (xor_9_out, not_81_out, and_191_out);
  and and_183 (and_183_out, not_81_out, and_191_out);
  and and_184 (and_184_out, not_75_out, not_76_out, not_77_out, not_78_out);
  and and_185 (and_185_out, d_ff_72_q, or_37_out);
  and and_186 (and_186_out, d_ff_74_q, or_37_out);
  and and_187 (and_187_out, d_ff_73_q, or_37_out);
  and and_188 (and_188_out, and_186_out, CMD);
  and and_189 (and_189_out, and_187_out, CMD);
  and and_190 (and_190_out, and_185_out, CMD);
  not not_79 (not_79_out, and_190_out);
  not not_80 (not_80_out, and_188_out);
  not not_81 (not_81_out, and_189_out);
  and and_191 (and_191_out, not_80_out, and_194_out);
  xor xor_10 (xor_10_out, not_80_out, and_194_out);
  and Neg (Neg_out, or_43_out, and_168_out);
  not not_82 (not_82_out, or_43_out);
  and Pos (Pos_out, not_82_out, not_83_out);
  not not_83 (not_83_out, and_168_out);
  not not_84 (not_84_out, or_43_out);
  and and_192 (and_192_out, d_ff_75_q, or_37_out);
  and and_193 (and_193_out, and_192_out, CMD);
  not not_85 (not_85_out, and_193_out);
  xor xor_11 (xor_11_out, not_85_out, 1'b1);
  and and_194 (and_194_out, not_85_out, 1'b1);
  and and_195 (and_195_out, xor_2_out, Neg_out);
  and and_196 (and_196_out, Pos_out, xor_2_out);
  and and_197 (and_197_out, not_86_out, not_84_out, or_40_out);
  not not_86 (not_86_out, CMD);
  and and_198 (and_198_out, and_184_out, Clock);
  or or_48 (or_48_out, and_197_out, and_196_out, and_200_out);
  and and_199 (and_199_out, and_128_out, Clock);
  not not_87 (not_87_out, or_40_out);
  and and_200 (and_200_out, and_195_out, not_87_out);
  not not_88 (not_88_out, and_198_out);
  and notZero (notZero_out, or_48_out, not_88_out);
  D_Flip_Flop d_ff_89 (.D(d_ff_68_q), .clk(and_199_out), .Q(d_ff_89_q));  // open: Qn, preset, reset
  D_Flip_Flop d_ff_90 (.D(d_ff_69_q), .clk(and_199_out), .Q(d_ff_90_q));  // open: Qn, preset, reset
  D_Flip_Flop d_ff_91 (.D(d_ff_70_q), .clk(and_199_out), .Q(d_ff_91_q));  // open: Qn, preset, reset
  D_Flip_Flop d_ff_92 (.D(d_ff_71_q), .clk(and_199_out), .Q(d_ff_92_q));  // open: Qn, preset, reset
  and and_201 (Zero, or_38_out, and_198_out);
  and and_202 (Negative, or_38_out, xor_2_out);
  and and_203 (Overflow, or_38_out, notZero_out);
  or or_49 (or_49_out, in_5, d_ff_89_q);
  or or_50 (or_50_out, in_6, d_ff_90_q);
  or or_51 (or_51_out, in_7, d_ff_91_q);
  or or_52 (or_52_out, in_8, d_ff_92_q);
  or or_53 (or_53_out, read_RAM, not_89_out);
  not not_89 (not_89_out, write_RAM);
  or or_54 (or_54_out, read_RAM, write_RAM);
  and and_204 (and_204_out, or_54_out, Clock);
  D_Flip_Flop d_ff_93 (.D(or_53_out), .clk(and_204_out), .Q(d_ff_93_q));  // open: Qn, preset, reset
  or or_55 (or_55_out, in_4, d_ff_51_q);
  not not_90 (not_90_out, or_55_out);
  not not_91 (not_91_out, d_ff_93_q);
  not not_92 (not_92_out, d_ff_93_q);
  and and_205 (and_205_out, or_55_out, not_91_out, or_49_out);
  and and_206 (and_206_out, or_55_out, not_91_out);
  and and_207 (and_207_out, not_92_out, not_90_out, or_49_out);
  and and_208 (and_208_out, not_90_out, not_92_out);
  or or_56 (or_56_out, and_209_out, and_210_out);
  and and_209 (and_209_out, or_55_out, d_ff_93_q, d_ff_94_q);
  D_Flip_Flop #(.trigger("high")) d_ff_94 (
    .D(and_205_out), .clk(and_206_out), .Q(d_ff_94_q));  // open: Qn, preset, reset
  D_Flip_Flop #(.trigger("high")) d_ff_95 (
    .D(and_207_out), .clk(and_208_out), .Q(d_ff_95_q));  // open: Qn, preset, reset
  and and_210 (and_210_out, not_90_out, d_ff_93_q, d_ff_95_q);
  not not_93 (not_93_out, d_ff_93_q);
  and and_211 (and_211_out, or_55_out, not_93_out, or_50_out);
  not not_94 (not_94_out, d_ff_93_q);
  D_Flip_Flop #(.trigger("high")) d_ff_96 (
    .D(and_211_out), .clk(and_212_out), .Q(d_ff_96_q));  // open: Qn, preset, reset
  and and_212 (and_212_out, or_55_out, not_93_out);
  D_Flip_Flop #(.trigger("high")) d_ff_97 (
    .D(and_213_out), .clk(and_214_out), .Q(d_ff_97_q));  // open: Qn, preset, reset
  and and_213 (and_213_out, not_94_out, not_90_out, or_50_out);
  and and_214 (and_214_out, not_94_out, not_90_out);
  or or_57 (or_57_out, and_215_out, and_216_out);
  and and_215 (and_215_out, or_55_out, d_ff_93_q, d_ff_96_q);
  and and_216 (and_216_out, not_90_out, d_ff_93_q, d_ff_97_q);
  not not_95 (not_95_out, d_ff_93_q);
  not not_96 (not_96_out, d_ff_93_q);
  D_Flip_Flop #(.trigger("high")) d_ff_98 (
    .D(and_217_out), .clk(and_218_out), .Q(d_ff_98_q));  // open: Qn, preset, reset
  and and_217 (and_217_out, or_55_out, not_95_out, or_51_out);
  and and_218 (and_218_out, or_55_out, not_95_out);
  D_Flip_Flop #(.trigger("high")) d_ff_99 (
    .D(and_219_out), .clk(and_220_out), .Q(d_ff_99_q));  // open: Qn, preset, reset
  and and_219 (and_219_out, not_96_out, not_90_out, or_51_out);
  and and_220 (and_220_out, not_96_out, not_90_out);
  or or_58 (or_58_out, and_221_out, and_222_out);
  and and_221 (and_221_out, or_55_out, d_ff_93_q, d_ff_98_q);
  and and_222 (and_222_out, not_90_out, d_ff_93_q, d_ff_99_q);
  not not_97 (not_97_out, d_ff_93_q);
  and and_223 (and_223_out, or_55_out, not_97_out, or_52_out);
  not not_98 (not_98_out, d_ff_93_q);
  and and_224 (and_224_out, not_98_out, not_90_out, or_52_out);
  and and_225 (and_225_out, or_55_out, d_ff_93_q, d_ff_100_q);
  D_Flip_Flop #(.trigger("high")) d_ff_100 (
    .D(and_223_out), .clk(and_226_out), .Q(d_ff_100_q));  // open: Qn, preset, reset
  and and_226 (and_226_out, or_55_out, not_97_out);
  D_Flip_Flop #(.trigger("high")) d_ff_101 (
    .D(and_224_out), .clk(and_227_out), .Q(d_ff_101_q));  // open: Qn, preset, reset
  and and_227 (and_227_out, not_98_out, not_90_out);
  or or_59 (or_59_out, and_225_out, and_228_out);
  and and_228 (and_228_out, not_90_out, d_ff_93_q, d_ff_101_q);
  and and_229 (and_229_out, read_RAM, Clock);
  D_Flip_Flop #(.trigger("falling")) d_ff_102 (
    .D(or_56_out), .clk(and_229_out), .Q(d_ff_102_q));  // open: Qn, preset, reset
  D_Flip_Flop #(.trigger("falling")) d_ff_103 (
    .D(or_57_out), .clk(and_229_out), .Q(d_ff_103_q));  // open: Qn, preset, reset
  D_Flip_Flop #(.trigger("falling")) d_ff_104 (
    .D(or_58_out), .clk(and_229_out), .Q(d_ff_104_q));  // open: Qn, preset, reset
  D_Flip_Flop #(.trigger("falling")) d_ff_105 (
    .D(or_59_out), .clk(and_229_out), .Q(d_ff_105_q));  // open: Qn, preset, reset

  // Notes on the sheet:
  //   PC
  //   Adress Input Pins
  //   Mode input pin
  //   4-bit data input pins
  //   Instruction RAM
  //   PC incrementer
  //   fetch 
  //   null, 1 = do nothing 
  //   1=run
  //   0=fetch
  //   instruction Register
  //   Stage 4 = Step 3: write to RB
  //   Register Input Pins
  //   CU = 1 is from ALU
  //   CU = 0 is from data RAM
  //   NOTE ABOUT STEP COUNTER/PIPELINE STAGES
  //   Stage 1 = Step 0 (with fetch = 1): RB to ALU
  //   Stage 2 = Step 1: ALU update status and A-out
  //   Stage 3 = Step 2: write/load to data RAM or overwrite PC
  //   temp (opcode)
  //   mode: 0=write, 1=read
  //   Stage 0 = Step 0 (with fetch = 0): PC -> IR RAM, update IR 
  //   Control Unit
  //   Step counter
  //   feed r0 to PC
  //   overwrite PC
  //   N/A
  //   N/A
  //   N/A
  //   Write to RB 
  //   N/A
  //   N/A
  //   Write to RB 
  //   N/A
  //   Write to RB 
  //   read jump address from r0
  //   RAM TO DATA OUT
  //   REG INPUT
  //   RAM load to data out
  //   RB load to data out
  //   data out to data in
  //   Write to data RAM
  //   RB load to L and R
  //   RB load to L and R
  //   REGISTER BLOCK
  //   Step incrementer
  //   carry 1
  //   Send add command, update status and A-out
  //   Send sub command, update status and A-out
  //   r1
  //   r0
  //   carry 2
  //   sum 1
  //   sum 2
  //   data out 1
  //   data out 2
  //   0 add, 1 sub
  //   L input
  //   ALU
  //   incremented PC
  //   jump address
  //   Adder
  //   updated PC
  //   R input
  //   2's Complement
  //   Data RAM Input Pins
  //   Data RAM Input Pins
  //   Data RAM Input Pins
  //   Data RAM Input Pins
  //   Status output
  //   -8 + -8 is underflow (not supported)
  //   tio load this needs to be 1
  //   mode: 0=write, 1=read
  //   address input pin
  //   address 1
  //   address 0
  //   DATA RAM
  //   data out 1
endmodule
