// Logisim project a5.circ as structural Verilog: 1 circuit, main circuit main
module main (
  input  mode,
  input  in_2,
  input  address,
  input  in_4,
  input  in_5,
  input  data_in,
  input  in_7,
  input  in_8,
  output out_9,
  output out_10,
  output out_11,
  output out_12
);

  wire and_1_out, and_2_out, and_3_out, and_4_out, and_5_out, and_6_out, and_7_out, and_8_out, and_9_out,
       and_10_out, and_11_out, and_12_out, and_13_out, and_14_out, and_15_out, and_16_out, and_17_out,
       and_18_out, and_19_out, and_20_out, and_21_out, and_22_out, and_23_out, and_24_out, and_25_out,
       and_26_out, and_27_out, and_28_out, and_29_out, and_30_out, and_31_out, and_32_out, and_33_out,
       and_34_out, and_35_out, and_36_out, and_37_out, and_38_out, and_39_out, and_40_out, and_41_out,
       and_42_out, and_43_out, and_44_out, and_45_out, and_46_out, and_47_out, and_48_out, and_49_out,
       and_50_out, and_51_out, and_52_out, and_53_out, and_54_out, and_55_out, and_56_out, and_57_out,
       and_58_out, and_59_out, and_60_out, and_61_out, and_62_out, and_63_out, and_64_out, and_65_out,
       and_66_out, and_67_out, and_68_out, and_69_out, and_70_out, and_71_out, and_72_out, and_73_out,
       and_74_out, and_75_out, and_76_out, clock_1_out, controlled_buffer_1_out, controlled_buffer_2_out,
       controlled_buffer_3_out, controlled_buffer_4_out, controlled_buffer_5_out, controlled_buffer_6_out,
       controlled_buffer_7_out, controlled_buffer_8_out, controlled_buffer_9_out, controlled_buffer_10_out,
       controlled_buffer_11_out, controlled_buffer_12_out, controlled_buffer_13_out,
       controlled_buffer_14_out, controlled_buffer_15_out, controlled_buffer_16_out,
       controlled_buffer_17_out, controlled_buffer_18_out, controlled_buffer_19_out,
       controlled_buffer_20_out, controlled_buffer_21_out, controlled_buffer_22_out,
       controlled_buffer_23_out, controlled_buffer_24_out, controlled_buffer_25_out,
       controlled_buffer_26_out, controlled_buffer_27_out, controlled_buffer_28_out,
       controlled_buffer_29_out, controlled_buffer_30_out, controlled_buffer_31_out,
       controlled_buffer_32_out, d_ff_1_q, d_ff_2_q, d_ff_3_q, d_ff_4_q, d_ff_5_q, d_ff_6_q, d_ff_7_q,
       d_ff_8_q, d_ff_9_q, d_ff_10_q, d_ff_11_q, d_ff_12_q, d_ff_13_q, d_ff_14_q, d_ff_15_q, d_ff_16_q,
       d_ff_18_q, d_ff_19_q, d_ff_20_q, d_ff_21_q, d_ff_22_q, d_ff_23_q, d_ff_24_q, d_ff_25_q, d_ff_27_q,
       d_ff_28_q, d_ff_29_q, d_ff_30_q, d_ff_31_q, d_ff_32_q, d_ff_33_q, d_ff_34_q, d_ff_36_q, d_ff_37_q,
       d_ff_38_q, d_ff_39_q, d_ff_40_q, d_ff_41_q, d_ff_42_q, d_ff_43_q, not_1_out, not_2_out, not_3_out,
       not_4_out, not_5_out, not_6_out, not_7_out, not_8_out, not_9_out, not_10_out, not_11_out, not_12_out,
       not_13_out, not_14_out, not_15_out, not_16_out, not_17_out, not_18_out, not_19_out, not_20_out,
       not_21_out, not_22_out, not_23_out, not_24_out, not_25_out, not_26_out, not_27_out, not_28_out,
       not_29_out, not_30_out, not_31_out, not_32_out, not_33_out, not_34_out, not_35_out, not_36_out,
       not_37_out, not_38_out, not_39_out, not_40_out, not_41_out, not_42_out, not_43_out, not_44_out,
       not_45_out, not_46_out, not_47_out, not_48_out, not_49_out, not_50_out, not_51_out, not_52_out,
       not_53_out, not_54_out, not_55_out, not_56_out, not_57_out, not_58_out, not_59_out, not_60_out,
       not_61_out, not_62_out, not_63_out, not_64_out, not_65_out, not_66_out, not_67_out, not_68_out,
       not_69_out, not_70_out, not_71_out, not_72_out, not_73_out, not_74_out, not_75_out, not_76_out,
       or_1_out, or_2_out, or_3_out, or_4_out;

  D_Flip_Flop d_ff_1 (.D(mode), .clk(clock_1_out), .Q(d_ff_1_q));  // open: Qn, preset, reset
  D_Flip_Flop d_ff_2 (.D(in_2), .clk(clock_1_out), .Q(d_ff_2_q));  // open: Qn, preset, reset
  D_Flip_Flop d_ff_3 (.D(address), .clk(clock_1_out), .Q(d_ff_3_q));  // open: Qn, preset, reset
  D_Flip_Flop d_ff_4 (.D(in_4), .clk(clock_1_out), .Q(d_ff_4_q));  // open: Qn, preset, reset
  not not_1 (not_1_out, d_ff_4_q);
  not not_2 (not_2_out, d_ff_3_q);
  not not_3 (not_3_out, d_ff_3_q);
  not not_4 (not_4_out, d_ff_4_q);
  not not_5 (not_5_out, d_ff_2_q);
  not not_6 (not_6_out, d_ff_2_q);
  not not_7 (not_7_out, d_ff_4_q);
  not not_8 (not_8_out, d_ff_2_q);
  not not_9 (not_9_out, d_ff_3_q);
  not not_10 (not_10_out, d_ff_2_q);
  not not_11 (not_11_out, d_ff_3_q);
  not not_12 (not_12_out, d_ff_4_q);
  and and_1 (and_1_out, d_ff_4_q, d_ff_3_q, d_ff_2_q);
  and and_2 (and_2_out, not_1_out, d_ff_3_q, d_ff_2_q);
  and and_3 (and_3_out, d_ff_2_q, not_2_out, d_ff_4_q);
  and and_4 (and_4_out, d_ff_2_q, not_3_out, not_4_out);
  and and_5 (and_5_out, not_5_out, d_ff_3_q, d_ff_4_q);
  and and_6 (and_6_out, not_6_out, d_ff_3_q, not_7_out);
  and and_7 (and_7_out, not_8_out, not_9_out, d_ff_4_q);
  and and_8 (and_8_out, not_10_out, not_11_out, not_12_out);
  D_Flip_Flop d_ff_5 (.D(in_5), .clk(clock_1_out), .Q(d_ff_5_q));  // open: Qn, preset, reset
  D_Flip_Flop d_ff_6 (.D(data_in), .clk(clock_1_out), .Q(d_ff_6_q));  // open: Qn, preset, reset
  D_Flip_Flop d_ff_7 (.D(in_7), .clk(clock_1_out), .Q(d_ff_7_q));  // open: Qn, preset, reset
  Clock clock_1 (.out(clock_1_out));
  D_Flip_Flop d_ff_8 (.D(in_8), .clk(clock_1_out), .Q(d_ff_8_q));  // open: Qn, preset, reset
  not not_13 (not_13_out, d_ff_1_q);
  not not_14 (not_14_out, d_ff_1_q);
  not not_15 (not_15_out, d_ff_1_q);
  not not_16 (not_16_out, d_ff_1_q);
  not not_17 (not_17_out, d_ff_1_q);
  not not_18 (not_18_out, d_ff_1_q);
  not not_19 (not_19_out, d_ff_1_q);
  not not_20 (not_20_out, d_ff_1_q);
  not not_21 (not_21_out, d_ff_1_q);
  not not_22 (not_22_out, d_ff_1_q);
  not not_23 (not_23_out, d_ff_1_q);
  not not_24 (not_24_out, d_ff_1_q);
  not not_25 (not_25_out, d_ff_1_q);
  not not_26 (not_26_out, d_ff_1_q);
  not not_27 (not_27_out, d_ff_1_q);
  not not_28 (not_28_out, d_ff_1_q);
  D_Flip_Flop d_ff_9 (.D(controlled_buffer_1_out), .clk(clock_1_out), .Q(d_ff_9_q));  // open: Qn, preset, reset
  and and_9 (and_9_out, not_13_out, and_1_out, d_ff_5_q);
  assign controlled_buffer_1_out = not_14_out ? and_9_out : 1'bz;  // Controlled_Buffer controlled_buffer_1
  D_Flip_Flop d_ff_10 (.D(controlled_buffer_2_out), .clk(clock_1_out), .Q(d_ff_10_q));  // open: Qn, preset, reset
  and and_10 (and_10_out, not_15_out, and_2_out, d_ff_5_q);
  assign controlled_buffer_2_out = not_16_out ? and_10_out : 1'bz;  // Controlled_Buffer controlled_buffer_2
  D_Flip_Flop d_ff_11 (.D(controlled_buffer_3_out), .clk(clock_1_out), .Q(d_ff_11_q));  // open: Qn, preset, reset
  and and_11 (and_11_out, not_17_out, and_3_out, d_ff_5_q);
  assign controlled_buffer_3_out = not_18_out ? and_11_out : 1'bz;  // Controlled_Buffer controlled_buffer_3
  D_Flip_Flop d_ff_12 (.D(controlled_buffer_4_out), .clk(clock_1_out), .Q(d_ff_12_q));  // open: Qn, preset, reset
  and and_12 (and_12_out, not_19_out, and_4_out, d_ff_5_q);
  assign controlled_buffer_4_out = not_20_out ? and_12_out : 1'bz;  // Controlled_Buffer controlled_buffer_4
  D_Flip_Flop d_ff_13 (.D(controlled_buffer_5_out), .clk(clock_1_out), .Q(d_ff_13_q));  // open: Qn, preset, reset
  and and_13 (and_13_out, not_21_out, and_5_out, d_ff_5_q);
  assign controlled_buffer_5_out = not_22_out ? and_13_out : 1'bz;  // Controlled_Buffer controlled_buffer_5
  D_Flip_Flop d_ff_14 (.D(controlled_buffer_6_out), .clk(clock_1_out), .Q(d_ff_14_q));  // open: Qn, preset, reset
  and and_14 (and_14_out, not_23_out, and_6_out, d_ff_5_q);
  assign controlled_buffer_6_out = not_24_out ? and_14_out : 1'bz;  // Controlled_Buffer controlled_buffer_6
  D_Flip_Flop d_ff_15 (.D(controlled_buffer_7_out), .clk(clock_1_out), .Q(d_ff_15_q));  // open: Qn, preset, reset
  and and_15 (and_15_out, not_25_out, and_7_out, d_ff_5_q);
  assign controlled_buffer_7_out = not_26_out ? and_15_out : 1'bz;  // Controlled_Buffer controlled_buffer_7
  D_Flip_Flop d_ff_16 (.D(controlled_buffer_8_out), .clk(clock_1_out), .Q(d_ff_16_q));  // open: Qn, preset, reset
  and and_16 (and_16_out, not_27_out, and_8_out, d_ff_5_q);
  assign controlled_buffer_8_out = not_28_out ? and_16_out : 1'bz;  // Controlled_Buffer controlled_buffer_8
  and and_17 (and_17_out, clock_1_out, d_ff_1_q);
  or or_1 (or_1_out, and_18_out, and_19_out, and_20_out, and_21_out, and_22_out, and_23_out, and_24_out, and_25_out);
  and and_18 (and_18_out, d_ff_1_q, and_1_out, d_ff_9_q);
  and and_19 (and_19_out, d_ff_1_q, and_2_out, d_ff_10_q);
  and and_20 (and_20_out, d_ff_1_q, and_3_out, d_ff_11_q);
  and and_21 (and_21_out, d_ff_1_q, and_4_out, d_ff_12_q);
  and and_22 (and_22_out, d_ff_1_q, and_5_out, d_ff_13_q);
  and and_23 (and_23_out, d_ff_1_q, and_6_out, d_ff_14_q);
  and and_24 (and_24_out, d_ff_1_q, and_7_out, d_ff_15_q);
  and and_25 (and_25_out, d_ff_1_q, and_8_out, d_ff_16_q);
  D_Flip_Flop d_ff_17 (.D(or_1_out), .clk(and_17_out), .Q(out_12));  // open: Qn, preset, reset
  not not_29 (not_29_out, d_ff_1_q);
  not not_30 (not_30_out, d_ff_1_q);
  not not_31 (not_31_out, d_ff_1_q);
  not not_32 (not_32_out, d_ff_1_q);
  not not_33 (not_33_out, d_ff_1_q);
  not not_34 (not_34_out, d_ff_1_q);
  not not_35 (not_35_out, d_ff_1_q);
  not not_36 (not_36_out, d_ff_1_q);
  not not_37 (not_37_out, d_ff_1_q);
  not not_38 (not_38_out, d_ff_1_q);
  not not_39 (not_39_out, d_ff_1_q);
  not not_40 (not_40_out, d_ff_1_q);
  not not_41 (not_41_out, d_ff_1_q);
  not not_42 (not_42_out, d_ff_1_q);
  not not_43 (not_43_out, d_ff_1_q);
  D_Flip_Flop d_ff_18 (.D(controlled_buffer_9_out), .clk(clock_1_out), .Q(d_ff_18_q));  // open: Qn, preset, reset
  and and_26 (and_26_out, not_29_out, and_1_out, d_ff_6_q);
  assign controlled_buffer_9_out = not_44_out ? and_26_out : 1'bz;  // Controlled_Buffer controlled_buffer_9
  not not_44 (not_44_out, d_ff_1_q);
  D_Flip_Flop d_ff_19 (.D(controlled_buffer_10_out), .clk(clock_1_out), .Q(d_ff_19_q));  // open: Qn, preset, reset
  and and_27 (and_27_out, not_30_out, and_2_out, d_ff_6_q);
  assign controlled_buffer_10_out = not_31_out ? and_27_out : 1'bz;  // Controlled_Buffer controlled_buffer_10
  D_Flip_Flop d_ff_20 (.D(controlled_buffer_11_out), .clk(clock_1_out), .Q(d_ff_20_q));  // open: Qn, preset, reset
  and and_28 (and_28_out, not_32_out, and_3_out, d_ff_6_q);
  assign controlled_buffer_11_out = not_33_out ? and_28_out : 1'bz;  // Controlled_Buffer controlled_buffer_11
  D_Flip_Flop d_ff_21 (.D(controlled_buffer_12_out), .clk(clock_1_out), .Q(d_ff_21_q));  // open: Qn, preset, reset
  and and_29 (and_29_out, not_34_out, and_4_out, d_ff_6_q);
  assign controlled_buffer_12_out = not_35_out ? and_29_out : 1'bz;  // Controlled_Buffer controlled_buffer_12
  D_Flip_Flop d_ff_22 (.D(controlled_buffer_13_out), .clk(clock_1_out), .Q(d_ff_22_q));  // open: Qn, preset, reset
  and and_30 (and_30_out, not_36_out, and_5_out, d_ff_6_q);
  assign controlled_buffer_13_out = not_37_out ? and_30_out : 1'bz;  // Controlled_Buffer controlled_buffer_13
  D_Flip_Flop d_ff_23 (.D(controlled_buffer_14_out), .clk(clock_1_out), .Q(d_ff_23_q));  // open: Qn, preset, reset
  and and_31 (and_31_out, not_38_out, and_6_out, d_ff_6_q);
  assign controlled_buffer_14_out = not_39_out ? and_31_out : 1'bz;  // Controlled_Buffer controlled_buffer_14
  D_Flip_Flop d_ff_24 (.D(controlled_buffer_15_out), .clk(clock_1_out), .Q(d_ff_24_q));  // open: Qn, preset, reset
  and and_32 (and_32_out, not_40_out, and_7_out, d_ff_6_q);
  assign controlled_buffer_15_out = not_41_out ? and_32_out : 1'bz;  // Controlled_Buffer controlled_buffer_15
  D_Flip_Flop d_ff_25 (.D(controlled_buffer_16_out), .clk(clock_1_out), .Q(d_ff_25_q));  // open: Qn, preset, reset
  and and_33 (and_33_out, not_42_out, and_8_out, d_ff_6_q);
  assign controlled_buffer_16_out = not_43_out ? and_33_out : 1'bz;  // Controlled_Buffer controlled_buffer_16
  and and_34 (and_34_out, clock_1_out, d_ff_1_q);
  or or_2 (or_2_out, and_35_out, and_36_out, and_37_out, and_38_out, and_39_out, and_40_out, and_41_out, and_42_out);
  and and_35 (and_35_out, d_ff_1_q, and_1_out, d_ff_18_q);
  and and_36 (and_36_out, d_ff_1_q, and_2_out, d_ff_19_q);
  and and_37 (and_37_out, d_ff_1_q, and_3_out, d_ff_20_q);
  and and_38 (and_38_out, d_ff_1_q, and_4_out, d_ff_21_q);
  and and_39 (and_39_out, d_ff_1_q, and_5_out, d_ff_22_q);
  and and_40 (and_40_out, d_ff_1_q, and_6_out, d_ff_23_q);
  and and_41 (and_41_out, d_ff_1_q, and_7_out, d_ff_24_q);
  and and_42 (and_42_out, d_ff_1_q, and_8_out, d_ff_25_q);
  D_Flip_Flop d_ff_26 (.D(or_2_out), .clk(and_34_out), .Q(out_9));  // open: Qn, preset, reset
  not not_45 (not_45_out, d_ff_1_q);
  not not_46 (not_46_out, d_ff_1_q);
  not not_47 (not_47_out, d_ff_1_q);
  not not_48 (not_48_out, d_ff_1_q);
  not not_49 (not_49_out, d_ff_1_q);
  not not_50 (not_50_out, d_ff_1_q);
  not not_51 (not_51_out, d_ff_1_q);
  not not_52 (not_52_out, d_ff_1_q);
  not not_53 (not_53_out, d_ff_1_q);
  not not_54 (not_54_out, d_ff_1_q);
  not not_55 (not_55_out, d_ff_1_q);
  not not_56 (not_56_out, d_ff_1_q);
  not not_57 (not_57_out, d_ff_1_q);
  not not_58 (not_58_out, d_ff_1_q);
  not not_59 (not_59_out, d_ff_1_q);
  not not_60 (not_60_out, d_ff_1_q);
  D_Flip_Flop d_ff_27 (.D(controlled_buffer_17_out), .clk(clock_1_out), .Q(d_ff_27_q));  // open: Qn, preset, reset
  and and_43 (and_43_out, not_45_out, and_1_out, d_ff_7_q);
  assign controlled_buffer_17_out = not_46_out ? and_43_out : 1'bz;  // Controlled_Buffer controlled_buffer_17
  D_Flip_Flop d_ff_28 (.D(controlled_buffer_18_out), .clk(clock_1_out), .Q(d_ff_28_q));  // open: Qn, preset, reset
  and and_44 (and_44_out, not_47_out, and_2_out, d_ff_7_q);
  assign controlled_buffer_18_out = not_48_out ? and_44_out : 1'bz;  // Controlled_Buffer controlled_buffer_18
  D_Flip_Flop d_ff_29 (.D(controlled_buffer_19_out), .clk(clock_1_out), .Q(d_ff_29_q));  // open: Qn, preset, reset
  and and_45 (and_45_out, not_49_out, and_3_out, d_ff_7_q);
  assign controlled_buffer_19_out = not_50_out ? and_45_out : 1'bz;  // Controlled_Buffer controlled_buffer_19
  D_Flip_Flop d_ff_30 (.D(controlled_buffer_20_out), .clk(clock_1_out), .Q(d_ff_30_q));  // open: Qn, preset, reset
  and and_46 (and_46_out, not_51_out, and_4_out, d_ff_7_q);
  assign controlled_buffer_20_out = not_52_out ? and_46_out : 1'bz;  // Controlled_Buffer controlled_buffer_20
  D_Flip_Flop d_ff_31 (.D(controlled_buffer_21_out), .clk(clock_1_out), .Q(d_ff_31_q));  // open: Qn, preset, reset
  and and_47 (and_47_out, not_53_out, and_5_out, d_ff_7_q);
  assign controlled_buffer_21_out = not_54_out ? and_47_out : 1'bz;  // Controlled_Buffer controlled_buffer_21
  D_Flip_Flop d_ff_32 (.D(controlled_buffer_22_out), .clk(clock_1_out), .Q(d_ff_32_q));  // open: Qn, preset, reset
  and and_48 (and_48_out, not_55_out, and_6_out, d_ff_7_q);
  assign controlled_buffer_22_out = not_56_out ? and_48_out : 1'bz;  // Controlled_Buffer controlled_buffer_22
  D_Flip_Flop d_ff_33 (.D(controlled_buffer_23_out), .clk(clock_1_out), .Q(d_ff_33_q));  // open: Qn, preset, reset
  and and_49 (and_49_out, not_57_out, and_7_out, d_ff_7_q);
  assign controlled_buffer_23_out = not_58_out ? and_49_out : 1'bz;  // Controlled_Buffer controlled_buffer_23
  D_Flip_Flop d_ff_34 (.D(controlled_buffer_24_out), .clk(clock_1_out), .Q(d_ff_34_q));  // open: Qn, preset, reset
  and and_50 (and_50_out, not_59_out, and_8_out, d_ff_7_q);
  assign controlled_buffer_24_out = not_60_out ? and_50_out : 1'bz;  // Controlled_Buffer controlled_buffer_24
  and and_51 (and_51_out, clock_1_out, d_ff_1_q);
  and and_52 (and_52_out, d_ff_1_q, and_1_out, d_ff_27_q);
  and and_53 (and_53_out, d_ff_1_q, and_2_out, d_ff_28_q);
  and and_54 (and_54_out, d_ff_1_q, and_3_out, d_ff_29_q);
  and and_55 (and_55_out, d_ff_1_q, and_4_out, d_ff_30_q);
  and and_56 (and_56_out, d_ff_1_q, and_5_out, d_ff_31_q);
  and and_57 (and_57_out, d_ff_1_q, and_6_out, d_ff_32_q);
  and and_58 (and_58_out, d_ff_1_q, and_7_out, d_ff_33_q);
  and and_59 (and_59_out, d_ff_1_q, and_8_out, d_ff_34_q);
  D_Flip_Flop d_ff_35 (.D(or_3_out), .clk(and_51_out), .Q(out_10));  // open: Qn, preset, reset
  or or_3 (or_3_out, and_52_out, and_53_out, and_54_out, and_55_out, and_56_out, and_57_out, and_58_out, and_59_out);
  not not_61 (not_61_out, d_ff_1_q);
  not not_62 (not_62_out, d_ff_1_q);
  not not_63 (not_63_out, d_ff_1_q);
  not not_64 (not_64_out, d_ff_1_q);
  not not_65 (not_65_out, d_ff_1_q);
  not not_66 (not_66_out, d_ff_1_q);
  not not_67 (not_67_out, d_ff_1_q);
  not not_68 (not_68_out, d_ff_1_q);
  not not_69 (not_69_out, d_ff_1_q);
  not not_70 (not_70_out, d_ff_1_q);
  not not_71 (not_71_out, d_ff_1_q);
  not not_72 (not_72_out, d_ff_1_q);
  not not_73 (not_73_out, d_ff_1_q);
  not not_74 (not_74_out, d_ff_1_q);
  not not_75 (not_75_out, d_ff_1_q);
  not not_76 (not_76_out, d_ff_1_q);
  D_Flip_Flop d_ff_36 (.D(controlled_buffer_25_out), .clk(clock_1_out), .Q(d_ff_36_q));  // open: Qn, preset, reset
  and and_60 (and_60_out, not_61_out, and_1_out, d_ff_8_q);
  assign controlled_buffer_25_out = not_62_out ? and_60_out : 1'bz;  // Controlled_Buffer controlled_buffer_25
  D_Flip_Flop d_ff_37 (.D(controlled_buffer_26_out), .clk(clock_1_out), .Q(d_ff_37_q));  // open: Qn, preset, reset
  and and_61 (and_61_out, not_63_out, and_2_out, d_ff_8_q);
  assign controlled_buffer_26_out = not_64_out ? and_61_out : 1'bz;  // Controlled_Buffer controlled_buffer_26
  D_Flip_Flop d_ff_38 (.D(controlled_buffer_27_out), .clk(clock_1_out), .Q(d_ff_38_q));  // open: Qn, preset, reset
  and and_62 (and_62_out, not_65_out, and_3_out, d_ff_8_q);
  assign controlled_buffer_27_out = not_66_out ? and_62_out : 1'bz;  // Controlled_Buffer controlled_buffer_27
  D_Flip_Flop d_ff_39 (.D(controlled_buffer_28_out), .clk(clock_1_out), .Q(d_ff_39_q));  // open: Qn, preset, reset
  and and_63 (and_63_out, not_67_out, and_4_out, d_ff_8_q);
  assign controlled_buffer_28_out = not_68_out ? and_63_out : 1'bz;  // Controlled_Buffer controlled_buffer_28
  D_Flip_Flop d_ff_40 (.D(controlled_buffer_29_out), .clk(clock_1_out), .Q(d_ff_40_q));  // open: Qn, preset, reset
  and and_64 (and_64_out, not_69_out, and_5_out, d_ff_8_q);
  assign controlled_buffer_29_out = not_70_out ? and_64_out : 1'bz;  // Controlled_Buffer controlled_buffer_29
  D_Flip_Flop d_ff_41 (.D(controlled_buffer_30_out), .clk(clock_1_out), .Q(d_ff_41_q));  // open: Qn, preset, reset
  and and_65 (and_65_out, not_71_out, and_6_out, d_ff_8_q);
  assign controlled_buffer_30_out = not_72_out ? and_65_out : 1'bz;  // Controlled_Buffer controlled_buffer_30
  D_Flip_Flop d_ff_42 (.D(controlled_buffer_31_out), .clk(clock_1_out), .Q(d_ff_42_q));  // open: Qn, preset, reset
  and and_66 (and_66_out, not_73_out, and_7_out, d_ff_8_q);
  assign controlled_buffer_31_out = not_74_out ? and_66_out : 1'bz;  // Controlled_Buffer controlled_buffer_31
  D_Flip_Flop d_ff_43 (.D(controlled_buffer_32_out), .clk(clock_1_out), .Q(d_ff_43_q));  // open: Qn, preset, reset
  and and_67 (and_67_out, not_75_out, and_8_out, d_ff_8_q);
  assign controlled_buffer_32_out = not_76_out ? and_67_out : 1'bz;  // Controlled_Buffer controlled_buffer_32
  and and_68 (and_68_out, clock_1_out, d_ff_1_q);
  and and_69 (and_69_out, d_ff_1_q, and_1_out, d_ff_36_q);
  and and_70 (and_70_out, d_ff_1_q, and_2_out, d_ff_37_q);
  and and_71 (and_71_out, d_ff_1_q, and_3_out, d_ff_38_q);
  and and_72 (and_72_out, d_ff_1_q, and_4_out, d_ff_39_q);
  and and_73 (and_73_out, d_ff_1_q, and_5_out, d_ff_40_q);
  and and_74 (and_74_out, d_ff_1_q, and_6_out, d_ff_41_q);
  and and_75 (and_75_out, d_ff_1_q, and_7_out, d_ff_42_q);
  and and_76 (and_76_out, d_ff_1_q, and_8_out, d_ff_43_q);
  D_Flip_Flop d_ff_44 (.D(or_4_out), .clk(and_68_out), .Q(out_11));  // open: Qn, preset, reset
  or or_4 (or_4_out, and_69_out, and_70_out, and_71_out, and_72_out, and_73_out, and_74_out, and_75_out, and_76_out);

  // Notes on the sheet:
  //   clock
  //   data out
endmodule
